// Logisim project Adder.circ as structural Verilog: 4 circuits, main circuit 半加器自动生成
module \半加器自动生成  (
  input  A,
  input  B,
  output Co,
  output S
);

  wire and_2_out, and_3_out, not_1_out, not_2_out;

  and and_1 (Co, A, B);
  not not_1 (not_1_out, A);
  and and_2 (and_2_out, not_1_out, B);
  not not_2 (not_2_out, B);
  and and_3 (and_3_out, not_2_out, A);
  or or_1 (S, and_2_out, and_3_out);
endmodule

// FA
module \手绘全加器  (
  input  Ai,
  input  Bi,
  input  Cin,
  output Si,
  output Cout
);

  wire and_1_out, and_2_out, and_3_out;

  xor xor_1 (Si, Ai, Bi, Cin);
  and and_1 (and_1_out, Ai, Bi);
  and and_2 (and_2_out, Ai, Cin);
  and and_3 (and_3_out, Bi, Cin);
  or or_1 (Cout, and_1_out, and_2_out, and_3_out);

  // Other names for the same wires on the sheet: Ci = Cin; Co = Cout

  // Notes on the sheet:
  //   输入引脚
  //   请勿增加、删除引脚，用隧道标签构建电路
  //   注意不要使用“组合逻辑分析”工具自动生成电路，自动生成会改变电路配置和封装外观！这将导致电路无法在educoder上完成测试。
  //   输出引脚
  //   请勿更改电路封装外观
endmodule

// 4位加法
module \_4位行波进位加法器  (
  input  [3:0] X,
  input  [3:0] Y,
  input  Cin,
  output [3:0] Sum,
  output Cout
);

  wire \手绘全加器_2_cout , \手绘全加器_3_cout , \手绘全加器_4_cout ;

  \手绘全加器  \u_手绘全加器_1  (.Ai(X[3]), .Bi(Y[3]), .Cin(\手绘全加器_2_cout ), .Si(Sum[3]), .Cout(Cout));
  \手绘全加器  \u_手绘全加器_2  (.Ai(X[2]), .Bi(Y[2]), .Cin(\手绘全加器_3_cout ), .Si(Sum[2]), .Cout(\手绘全加器_2_cout ));
  \手绘全加器  \u_手绘全加器_3  (.Ai(X[1]), .Bi(Y[1]), .Cin(\手绘全加器_4_cout ), .Si(Sum[1]), .Cout(\手绘全加器_3_cout ));
  \手绘全加器  \u_手绘全加器_4  (.Ai(X[0]), .Bi(Y[0]), .Cin(Cin), .Si(Sum[0]), .Cout(\手绘全加器_4_cout ));
  // Probe on X
  // Probe on Y
  // Probe on Sum
  // Probe on X
  // Probe on Y
  // Probe on Sum

  // Other names for the same wires on the sheet: Ci = Cin; Co = Cout; S[3:0] = Sum; S0 = Sum[0]; S1 = Sum[1];
  //   S2 = Sum[2]; S3 = Sum[3]

  // Notes on the sheet:
  //   Y: pull=down
  //   Cin: pull=down
  //   X: pull=down
  //   输入引脚区
  //   输出引脚区
  //   功能说明:4位串行加法器 S=X+Y+Cin，Cout为最高位进位，Cin为进位输入
  //   +
  //   =
  //   有符号加法
  //   +
  //   =
  //   无符号加法
endmodule

// 1位BCD加法
module \_1位十进制加法器  (
  input  [3:0] X,
  input  [3:0] Y,
  input  Cin,
  output Cout,
  output [3:0] Sum
);

  wire and_1_out, and_2_out, \n4位行波进位加法器_2_cout ;
  wire [3:0] \n4位行波进位加法器_2_sum , undriven;

  or or_1 (Cout, and_1_out, and_2_out, \n4位行波进位加法器_2_cout );
  and and_1 (and_1_out, \n4位行波进位加法器_2_sum [1], \n4位行波进位加法器_2_sum [3]);
  \_4位行波进位加法器  \u_4位行波进位加法器_1  (
    .X({undriven[3], {2{Cout}}, undriven[0]}), .Y(\n4位行波进位加法器_2_sum ), .Sum(Sum));  // open: Cin, Cout
  \_4位行波进位加法器  \u_4位行波进位加法器_2  (.X(X), .Y(Y), .Cin(Cin), .Sum(\n4位行波进位加法器_2_sum ), .Cout(\n4位行波进位加法器_2_cout ));
  Hex_Digit_Display hex_digit_display_1 (.value(X));  // open: dp
  and and_2 (and_2_out, \n4位行波进位加法器_2_sum [3], \n4位行波进位加法器_2_sum [2]);
  Hex_Digit_Display hex_digit_display_2 (.value(Y));  // open: dp
  Hex_Digit_Display hex_digit_display_3 (.value({3'b000, Cin}));  // open: dp
  Hex_Digit_Display hex_digit_display_4 (.value({3'b000, Cout}));  // open: dp
  Hex_Digit_Display hex_digit_display_5 (.value(Sum));  // open: dp

  // Other names for the same wires on the sheet: Ci = Cin; Co = Cout; S[3:0] = Sum

  // Notes on the sheet:
  //   Y: pull=down
  //   Cin: pull=down
  //   X: pull=down
  //   输入引脚区
  //   输出引脚区
  //   功能说明:1位BCD码加法器 S=X+Y+Cin，Cout为进位输出，Cin为进位输入
  //   +
  //   +
  //   测试监控区
  //   =
endmodule
