// Logisim project Comparer.circ as structural Verilog: 5 circuits, main circuit 1位比较器
module \_1位比较器  (
  input  X,
  input  Y,
  output Great,
  output Equal,
  output Less
);

  wire not_1_out, xor_1_out;

  xor xor_1 (xor_1_out, X, Y);
  not not_1 (not_1_out, Y);
  and and_1 (Great, not_1_out, X);
  not not_2 (Equal, xor_1_out);
  nor nor_1 (Less, Equal, Great);

  // Notes on the sheet:
  //   电路功能：X,Y进行比较，Great=(X>Y)?1:0;
  //   输入引脚区
  //   输出引脚区
endmodule

module \_2位比较器  (
  input  [1:0] X,
  input  [1:0] Y,
  output Great,
  output Equal,
  output Less
);

  wire and_1_out, and_3_out, \n1位比较器_1_equal , \n1位比较器_1_great , \n1位比较器_1_less , \n1位比较器_2_equal ,
       \n1位比较器_2_great , \n1位比较器_2_less ;

  // Probe on X
  // Probe on Y
  \_1位比较器  \u_1位比较器_1  (.X(X[1]), .Y(Y[1]), .Great(\n1位比较器_1_great ), .Equal(\n1位比较器_1_equal ), .Less(\n1位比较器_1_less ));
  \_1位比较器  \u_1位比较器_2  (.X(X[0]), .Y(Y[0]), .Great(\n1位比较器_2_great ), .Equal(\n1位比较器_2_equal ), .Less(\n1位比较器_2_less ));
  and and_1 (and_1_out, \n1位比较器_1_equal , \n1位比较器_2_great );
  and and_2 (Equal, \n1位比较器_1_equal , \n1位比较器_2_equal );
  and and_3 (and_3_out, \n1位比较器_1_equal , \n1位比较器_2_less );
  or or_1 (Less, and_3_out, \n1位比较器_1_less );
  or or_2 (Great, \n1位比较器_1_great , and_1_out);

  // Notes on the sheet:
  //   电路功能：X,Y进行无符号比较，Great=(X>Y)?1:0;
  //   输入引脚区
  //   输出引脚区
endmodule

// 4位比较
module \_4位无符号比较器  (
  input  [3:0] X,
  input  [3:0] Y,
  output Great,
  output Equal,
  output Less
);

  wire and_2_out, and_3_out, and_4_out, and_5_out, not_1_out, not_2_out, not_3_out, not_4_out, xnor_1_out,
       xnor_2_out, xnor_3_out, xnor_4_out;

  // Probe on X
  // Probe on Y
  xnor xnor_1 (xnor_1_out, X[3], Y[3]);
  xnor xnor_2 (xnor_2_out, X[2], Y[2]);
  xnor xnor_3 (xnor_3_out, X[1], Y[1]);
  xnor xnor_4 (xnor_4_out, X[0], Y[0]);
  not not_1 (not_1_out, Y[3]);
  not not_2 (not_2_out, Y[2]);
  not not_3 (not_3_out, Y[1]);
  not not_4 (not_4_out, Y[0]);
  and and_1 (Equal, xnor_1_out, xnor_2_out, xnor_3_out, xnor_4_out);
  and and_2 (and_2_out, not_1_out, X[3]);
  and and_3 (and_3_out, xnor_1_out, not_2_out, X[2]);
  and and_4 (and_4_out, xnor_1_out, xnor_2_out, not_3_out, X[1]);
  and and_5 (and_5_out, xnor_1_out, xnor_2_out, xnor_3_out, not_4_out, X[0]);
  or or_1 (Great, and_2_out, and_3_out, and_4_out, and_5_out);
  nor nor_1 (Less, Equal, Great);

  // Notes on the sheet:
  //   电路功能：X,Y进行无符号比较，Great=(X>Y)?1:0;
  //   输入引脚区
  //   输出引脚区
endmodule

module \_16位无符号比较器  (
  input  [15:0] X,
  input  [15:0] Y,
  output Great,
  output Equal,
  output Less
);

  wire and_1_out, and_2_out, and_3_out, and_4_out, and_5_out, and_7_out, \n4位无符号比较器_1_equal ,
       \n4位无符号比较器_1_great , \n4位无符号比较器_1_less , \n4位无符号比较器_2_equal , \n4位无符号比较器_2_great , \n4位无符号比较器_2_less ,
       \n4位无符号比较器_3_equal , \n4位无符号比较器_3_great , \n4位无符号比较器_3_less , \n4位无符号比较器_4_equal ,
       \n4位无符号比较器_4_great , \n4位无符号比较器_4_less ;

  // Probe on X
  // Probe on Y
  \_4位无符号比较器  \u_4位无符号比较器_1  (
    .X(X[15:12]), .Y(Y[15:12]), .Great(\n4位无符号比较器_1_great ), .Equal(\n4位无符号比较器_1_equal ),
    .Less(\n4位无符号比较器_1_less ));
  \_4位无符号比较器  \u_4位无符号比较器_2  (
    .X(X[11:8]), .Y(Y[11:8]), .Great(\n4位无符号比较器_2_great ), .Equal(\n4位无符号比较器_2_equal ),
    .Less(\n4位无符号比较器_2_less ));
  \_4位无符号比较器  \u_4位无符号比较器_3  (
    .X(X[7:4]), .Y(Y[7:4]), .Great(\n4位无符号比较器_3_great ), .Equal(\n4位无符号比较器_3_equal ),
    .Less(\n4位无符号比较器_3_less ));
  \_4位无符号比较器  \u_4位无符号比较器_4  (
    .X(X[3:0]), .Y(Y[3:0]), .Great(\n4位无符号比较器_4_great ), .Equal(\n4位无符号比较器_4_equal ),
    .Less(\n4位无符号比较器_4_less ));
  and and_1 (and_1_out, \n4位无符号比较器_2_equal , \n4位无符号比较器_1_equal , \n4位无符号比较器_3_great );
  and and_2 (and_2_out, \n4位无符号比较器_3_less , \n4位无符号比较器_2_equal , \n4位无符号比较器_1_equal );
  and and_3 (and_3_out, \n4位无符号比较器_1_equal , \n4位无符号比较器_2_great );
  and and_4 (and_4_out, \n4位无符号比较器_1_equal , \n4位无符号比较器_2_less );
  and and_5 (and_5_out, \n4位无符号比较器_1_equal , \n4位无符号比较器_2_equal , \n4位无符号比较器_3_equal , \n4位无符号比较器_4_great );
  and and_6 (Equal, \n4位无符号比较器_1_equal , \n4位无符号比较器_2_equal , \n4位无符号比较器_3_equal , \n4位无符号比较器_4_equal );
  and and_7 (and_7_out, \n4位无符号比较器_2_equal , \n4位无符号比较器_1_equal , \n4位无符号比较器_3_equal , \n4位无符号比较器_4_less );
  or or_1 (Great, \n4位无符号比较器_1_great , and_3_out, and_1_out, and_5_out);
  or or_2 (Less, \n4位无符号比较器_1_less , and_4_out, and_2_out, and_7_out);

  // Other names for the same wires on the sheet: X0[3:0] = X[3:0]; X1[3:0] = X[7:4]; X2[3:0] = X[11:8];
  //   X3[3:0] = X[15:12]; Y0[3:0] = Y[3:0]; Y1[3:0] = Y[7:4]; Y2[3:0] = Y[11:8]; Y3[3:0] = Y[15:12]

  // Notes on the sheet:
  //   电路功能：X,Y进行无符号比较，Great=(X>Y)?1:0;
  //   输入引脚区
  //   输出引脚区
endmodule

module \_16位无符号比较器自动测试  (
);

  wire and_1_out, CLK, comparator_2_eq, d_ff_1_q, d_ff_1_qn, Halt, NEQ;
  wire [2:0] comparator_1_gt, \n16位无符号比较器_1_great ;
  wire [7:0] counter_1_q;
  wire [9:0] counter_2_q;
  wire [15:0] multiplexer_1_out, multiplexer_1_out_2;
  wire [31:0] XY;

  Counter #(.ongoal("stay")) counter_1 (.Q(counter_1_q), .carry(Halt), .clk(CLK));  // open: load, D, count, clr
  Counter #(.width(10), .max('h3ff)) counter_2 (
    .count(NEQ), .Q(counter_2_q), .clk(CLK), .clr(Halt));  // open: load, D, carry
  LED \u_测试完成  (.in(Halt));
  and and_1 (and_1_out, ~Halt, NEQ);  // AND_Gate
  Clock clock_1 (.out(CLK));
  ROM #(.dataWidth(32)) rom_1 (.addr(counter_1_q), .data(XY));  // open: sel
  RAM #(.addrWidth(10), .dataWidth(32), .bus("separate")) ram_1 (
    .addr(counter_2_q), .din(XY), .str(and_1_out), .clk(CLK));  // open: data, sel, ld, clr
  _7_Segment_Display u_7_segment_display_1 (
    .g(multiplexer_1_out[15]), .f(multiplexer_1_out[14]), .a(multiplexer_1_out[13]),
    .b(multiplexer_1_out[12]), .e(multiplexer_1_out_2[15]), .d(multiplexer_1_out_2[14]),
    .c(multiplexer_1_out_2[13]), .dp(multiplexer_1_out_2[12]));
  _7_Segment_Display u_7_segment_display_2 (
    .g(multiplexer_1_out[11]), .f(multiplexer_1_out[10]), .a(multiplexer_1_out[9]), .b(multiplexer_1_out[8]),
    .e(multiplexer_1_out_2[11]), .d(multiplexer_1_out_2[10]), .c(multiplexer_1_out_2[9]),
    .dp(multiplexer_1_out_2[8]));
  D_Flip_Flop d_ff_1 (.clk(CLK), .D(NEQ), .Q(d_ff_1_q), .Qn(d_ff_1_qn), .en(d_ff_1_qn));  // open: preset, reset
  \_16位无符号比较器  \u_16位无符号比较器_1  (
    .X(XY[31:16]), .Y(XY[15:0]), .Great(\n16位无符号比较器_1_great [0]), .Equal(\n16位无符号比较器_1_great [1]),
    .Less(\n16位无符号比较器_1_great [2]));
  Comparator #(.width(16), .mode("unsigned")) comparator_1 (
    .a(XY[31:16]), .b(XY[15:0]), .gt(comparator_1_gt[0]), .eq(comparator_1_gt[1]), .lt(comparator_1_gt[2]));
  _7_Segment_Display u_7_segment_display_3 (
    .g(multiplexer_1_out[3]), .f(multiplexer_1_out[2]), .a(multiplexer_1_out[1]), .b(multiplexer_1_out[0]),
    .e(multiplexer_1_out_2[3]), .d(multiplexer_1_out_2[2]), .c(multiplexer_1_out_2[1]),
    .dp(multiplexer_1_out_2[0]));
  _7_Segment_Display u_7_segment_display_4 (
    .g(multiplexer_1_out[7]), .f(multiplexer_1_out[6]), .a(multiplexer_1_out[5]), .b(multiplexer_1_out[4]),
    .e(multiplexer_1_out_2[7]), .d(multiplexer_1_out_2[6]), .c(multiplexer_1_out_2[5]),
    .dp(multiplexer_1_out_2[4]));
  not not_1 (NEQ, comparator_2_eq);
  Comparator #(.width(3)) comparator_2 (
    .a(\n16位无符号比较器_1_great ), .b(comparator_1_gt), .eq(comparator_2_eq));  // open: gt, lt
  Multiplexer #(.width(32), .disabled(0)) multiplexer_1 (
    .in0(32'h8a66ffee), .in1(32'h8a8cef44), .out({multiplexer_1_out_2, multiplexer_1_out}), .sel(d_ff_1_q),
    .en(Halt));

  // Notes on the sheet:
  //   X&Y trace
  //   错误记录X&Y
  //   存储器保存未通过的测试用例
  //   contents of rom_1 (hex, n*v repeats v):
  //   ffffffff ffff7fff ffffbfff ffffdfff ffffefff f7fff7ff fffff7ff fffffbff fffffdff fffffeff ff7fff7f
  //   ff7fff7f ffffff7f ffffffbf ffffffdf ffffffef fff7fff7 fffffff7 fffffffb fffffffd fffffffe 0 1 2 4 8
  //   100010 10 20 40 80 1000100 100 200 400 800 10001000 1000 2000 4000 8000 f4815766 588f50e1 691a47b9
  //   953cad65 f4d07a42 847bfafc 699a478c d3a3b941 45a67aa3 40ad61ed fbdbd7af ad681465 6d29551b f8b4a89f
  //   c46931ce 6da641d0 a32356fb c8596d72 c8d957f6 a225ef12 e2f0e69e dac18d78 2c29b6da e8498992 849a8fa0
  //   cc89dbb9 96e7ac10 d859e7c7 ed1b931f 9a6b0c71 5dc43051 905b4680 fd993c02 dc7a144e e08fe5be 3d2cda1d
  //   3953372f b7c73bb4 9541ca16 a38833d4 66592fd4 11325f9 a28ecd02 2689baee 3995efa0 b7850caa f7bc8a4b
  //   72bf7a08 2f844308 b9c16ec6 d7bd681f 5f4f8054 be5e184 167473ff 78485951 969b16d7 e01899d1 8f5743fd
  //   86828397 40d809aa 6d2a022d 6eb919b 3df509cb 916d453a 8dec9f 119c9a28 a7ed3a2b 4f740789 8c5fdf2d
  //   76a8d8a9 3509609a e92e56c fa5bd025 82bad13 14987cde e37be3cc 173e6657 fd23792 99971ce1 42aae4e6
  //   b700fd56 133aa7c6 7779af1 fc95a98b dd69adbb 9bb14002 ed880001 c452a662 dab9962 ecf24c8d aaabc9e7
  //   70cfed22 eb57bbac 61cc4ee1 f043d59d 890769da d2a27dbd eff19cf0 8682ad82 3d31b42a 2064ebd d1fcb45b
  //   d20f7b97 85ccb489 9f8f8018 7b9e81b9 8ebddfc3 d15f5d7e d4a1a5be fc21dbd8 144ea10 c737b8e8 2fcaba65
  //   42e372f4 ee4378ec c3f48937 793c47c3 c117402 93843b6a a87fbeb1 6fc6d2d5 85fa1fea 95579780 713300af
  //   fdb7cc1c 346496c5 70fdb449 25338adf 22be43dc abe31724 f27ee841 99a69e81 15fea25d 26c1f149 bf4cb8c
  //   1533c7ab 45c1a42b a42a6e6d 222a2e30 2a5e3686 5caeda57 c02aab14 765acad5 4706d961 fe025b53 922c42e5
  //   b89287ec 70e6f79d 60622e31 d91c7840 cd0cd37 b1c0a92e 4b6f62a6 b10aebaf f62577cd 73fa0e0d aca68551
  //   f99276ec 233c77e6 c9cfc487 eac76497 39b70c27 19695f22 460dfa7d d920e8e0 367a4942 d3592c2 c4c152a6
  //   efda30d8 245dff15 6b7761ed 8b08ddc9 c54931b0 603fecac 181c3fed e6866805 8d2b1b5b 2f6dee84 68346271
  //   777e5a0b 7396c0d3 dd85e1d3 ff7203cb 688c6e5f 46c54453 9ca87bbe e2328930 17e67a9c 9051479b 5ba54a2
  //   604bccfb 747a8cad c050e030 6ee2674d 5e3bcceb 20c99c16 66b28f9a 3a294443 95fcfc62 22340f2a ed897fa6
  //   b11038fb 92a57aa5 91815453 5d7942a2 302bab20 8e1b6d1f bcbfcf4f 303557a5 c33fe7d1 5a8cbd9f 72e5a6e
  //   180cb2c6 9313a6e2 c5fc7c97
  //   16位数无符号比较器自动测试
  //   ctrl+K驱动时钟自动测试
endmodule
