// Logisim project DecoderLab.circ as structural Verilog: 4 circuits, main circuit Decoder2-4
// Dec24
module Decoder2_4 (
  input  A1,
  input  A0,
  input  Enable,
  output Y0,
  output Y2,
  output Y1,
  output Y3
);

  wire and_1_out, and_2_out, and_3_out, and_4_out, not_1_out, not_2_out;

  not not_1 (not_1_out, A1);
  not not_2 (not_2_out, A0);
  and and_1 (and_1_out, not_2_out, not_1_out);
  and and_2 (and_2_out, A0, not_1_out);
  and and_3 (and_3_out, not_2_out, A1);
  and and_4 (and_4_out, A0, A1);
  and and_5 (Y0, Enable, and_1_out);
  and and_6 (Y1, Enable, and_2_out);
  and and_7 (Y2, Enable, and_3_out);
  and and_8 (Y3, Enable, and_4_out);

  // Notes on the sheet:
  //   Enable: pull=down
  //   2线-4线译码器
  //   请不要改变封装外观，否则无法完成测试
endmodule

// Deocder38
module Decoder3_8 (
  input  A2,
  input  A1,
  input  A0,
  input  Enable,
  output Y0,
  output Y4,
  output Y1,
  output Y5,
  output Y2,
  output Y6,
  output Y3,
  output Y7
);

  wire and_1_out, and_2_out, not_1_out;

  not not_1 (not_1_out, A2);
  and and_1 (and_1_out, not_1_out, Enable);
  and and_2 (and_2_out, A2, Enable);
  Decoder2_4 decoder2_4_1 (.A1(A1), .Y0(Y0), .Y2(Y2), .A0(A0), .Y1(Y1), .Y3(Y3), .Enable(and_1_out));
  Decoder2_4 decoder2_4_2 (.A1(A1), .Y0(Y4), .Y2(Y6), .A0(A0), .Y1(Y5), .Y3(Y7), .Enable(and_2_out));

  // Notes on the sheet:
  //   Enable: pull=down
  //   3线-8线译码器
  //   请不要改变封装外观，否则无法完成测试
endmodule

module _74LS138 (
  input  A2,
  input  G1,
  input  A1,
  input  nG2a,
  input  A0,
  input  nG2b,
  output nY0,
  output nY4,
  output nY1,
  output nY5,
  output nY2,
  output nY6,
  output nY3,
  output nY7
);

  wire and_1_out, not_1_out, not_2_out, not_3_out, not_4_out, not_5_out;

  not not_1 (not_1_out, A2);
  not not_2 (not_2_out, A1);
  not not_3 (not_3_out, A0);
  not not_4 (not_4_out, nG2a);
  not not_5 (not_5_out, nG2b);
  and and_1 (and_1_out, G1, not_4_out, not_5_out);
  nand nand_1 (nY7, and_1_out, A0, A1, A2);
  nand nand_2 (nY6, and_1_out, not_3_out, A1, A2);
  nand nand_3 (nY5, and_1_out, A0, not_2_out, A2);
  nand nand_4 (nY4, and_1_out, not_3_out, not_2_out, A2);
  nand nand_5 (nY3, and_1_out, A0, A1, not_1_out);
  nand nand_6 (nY2, and_1_out, not_3_out, A1, not_1_out);
  nand nand_7 (nY1, and_1_out, A0, not_2_out, not_1_out);
  nand nand_8 (nY0, and_1_out, not_3_out, not_2_out, not_1_out);

  // Notes on the sheet:
  //   G1: pull=down
  //   nG2a: pull=down
  //   nG2b: pull=down
  //   3线-8线译码器：74LS138（低电平译码）
  //   请不要改变封装外观，否则无法完成测试
endmodule

module \译码器应用  (
  input  A,
  input  B,
  input  Enable,
  input  Ci,
  output Co,
  output Sum
);

  wire n74ls138_1_ny1, n74ls138_1_ny2, n74ls138_1_ny3, n74ls138_1_ny4, n74ls138_1_ny5, n74ls138_1_ny6,
       n74ls138_1_ny7, not_1_out, not_2_out;

  _74LS138 u_74ls138_1 (
    .A2(A), .G1(Enable), .nY4(n74ls138_1_ny4), .A1(B), .nG2a(not_1_out), .nY1(n74ls138_1_ny1),
    .nY5(n74ls138_1_ny5), .A0(Ci), .nG2b(not_2_out), .nY2(n74ls138_1_ny2), .nY6(n74ls138_1_ny6),
    .nY3(n74ls138_1_ny3), .nY7(n74ls138_1_ny7));  // open: nY0
  not not_1 (not_1_out, Enable);
  not not_2 (not_2_out, Enable);
  nand nand_1 (Sum, n74ls138_1_ny1, n74ls138_1_ny2, n74ls138_1_ny4, n74ls138_1_ny7);
  nand nand_2 (Co, n74ls138_1_ny3, n74ls138_1_ny5, n74ls138_1_ny6, n74ls138_1_ny7);

  // Notes on the sheet:
  //   Enable: pull=down
  //   使用3-8译码器配合适当的门构建全加器FA
  //   请不要改变封装外观，否则无法完成测试
endmodule
