// Logisim project Latch_Flipflop.circ as structural Verilog: 7 circuits, main circuit 基本锁存器
// bSR
module \基本锁存器  (
  input  R,
  input  S,
  output Qa,
  output Qb
);

  nor nor_1 (Qa, R, Qb);
  nor nor_2 (Qb, Qa, S);

  // Notes on the sheet:
  //   R: pull=down
  //   Qa: pull=down
  //   S: pull=down
  //   Qb: pull=down
  //   输入引脚
  //   请勿更改电路封装外观
  //   请勿增加、删除引脚，用隧道标签构建电路
  //   输出引脚
  //   武汉纺织大学数字逻辑课程组
endmodule

// cSR
module \门控SR锁存器  (
  input  R,
  input  CLK,
  input  S,
  output Q,
  output nQ
);

  wire and_1_out, and_2_out;

  and and_1 (and_1_out, R, CLK);
  and and_2 (and_2_out, CLK, S);
  nor nor_1 (Q, and_1_out, nQ);
  nor nor_2 (nQ, Q, and_2_out);

  // Notes on the sheet:
  //   CLK: pull=down
  //   R: pull=down
  //   Q: pull=down
  //   nQ: pull=down
  //   S: pull=down
  //   输入引脚
  //   请勿更改电路封装外观
  //   请勿增加、删除引脚，用隧道标签构建电路
  //   输出引脚
  //   武汉纺织大学数字逻辑课程组
endmodule

// ncSR
module \与非门构成的门控SR锁存器  (
  input  R,
  input  CLK,
  input  S,
  output Q,
  output nQ
);

  wire nand_1_out, nand_2_out;

  nand nand_1 (nand_1_out, R, CLK);
  nand nand_2 (nand_2_out, CLK, S);
  nand nand_3 (Q, nand_2_out, nQ);
  nand nand_4 (nQ, Q, nand_1_out);

  // Notes on the sheet:
  //   Q: pull=down
  //   CLK: pull=down
  //   nQ: pull=down
  //   R: pull=down
  //   S: pull=down
  //   输入引脚
  //   请勿更改电路封装外观
  //   请勿增加、删除引脚，用隧道标签构建电路
  //   输出引脚
  //   武汉纺织大学数字逻辑课程组
endmodule

// D_Latch
module \门控D锁存器  (
  input  D,
  input  CLK,
  output Q,
  output nQ
);

  wire not_1_out;

  not not_1 (not_1_out, D);
  \与非门构成的门控SR锁存器  \u_与非门构成的门控sr锁存器_1  (.R(not_1_out), .CLK(CLK), .S(D), .Q(Q), .nQ(nQ));

  // Notes on the sheet:
  //   nQ: pull=down
  //   D: pull=down
  //   Q: pull=down
  //   CLK: pull=down
  //   输入引脚
  //   请勿更改电路封装外观
  //   请勿增加、删除引脚，用隧道标签构建电路
  //   输出引脚
  //   武汉纺织大学数字逻辑课程组
endmodule

// DFF
module \主从D触发器_下降沿  (
  input  D,
  input  Clock,
  output Q,
  output nQ
);

  wire not_1_out, \门控d锁存器_1_q ;

  \门控D锁存器  \u_门控d锁存器_1  (.D(D), .CLK(Clock), .Q(\门控d锁存器_1_q ));  // open: nQ
  not not_1 (not_1_out, Clock);
  \门控D锁存器  \u_门控d锁存器_2  (.D(\门控d锁存器_1_q ), .CLK(not_1_out), .Q(Q), .nQ(nQ));

  // Notes on the sheet:
  //   nQ: pull=down
  //   Q: pull=down
  //   Clock: pull=down
  //   D: pull=down
  //   输入引脚
  //   请勿更改电路封装外观
  //   请勿增加、删除引脚，用隧道标签构建电路
  //   输出引脚
  //   武汉纺织大学数字逻辑课程组
endmodule

// TFF
module \T触发器  (
  input  T,
  input  Clock,
  output Q,
  output nQ
);

  wire and_1_out, and_2_out, not_1_out, not_2_out, or_1_out;

  not not_1 (not_1_out, T);
  and and_1 (and_1_out, Q, not_1_out);
  and and_2 (and_2_out, T, nQ);
  not not_2 (not_2_out, Clock);
  or or_1 (or_1_out, and_1_out, and_2_out);
  \主从D触发器_下降沿  \u_主从d触发器_下降沿_1  (.D(or_1_out), .Q(Q), .Clock(not_2_out), .nQ(nQ));

  // Notes on the sheet:
  //   输入引脚
  //   请勿更改电路封装外观
  //   请勿增加、删除引脚，用隧道标签构建电路
  //   输出引脚
  //   武汉纺织大学数字逻辑课程组
endmodule

// JKFF
module \JK触发器  (
  input  J,
  input  Clock,
  input  K,
  output Q,
  output nQ
);

  wire and_1_out, and_2_out, not_1_out, not_2_out, or_1_out;

  not not_1 (not_1_out, K);
  and and_1 (and_1_out, Q, not_1_out);
  and and_2 (and_2_out, J, nQ);
  or or_1 (or_1_out, and_1_out, and_2_out);
  not not_2 (not_2_out, Clock);
  \主从D触发器_下降沿  \u_主从d触发器_下降沿_1  (.D(or_1_out), .Q(Q), .Clock(not_2_out), .nQ(nQ));

  // Notes on the sheet:
  //   输入引脚
  //   请勿更改电路封装外观
  //   请勿增加、删除引脚，用隧道标签构建电路
  //   输出引脚
  //   武汉纺织大学数字逻辑课程组
endmodule
