// Logisim project LogicFuncTools.circ as structural Verilog: 5 circuits, main circuit 布尔表达式
// Bool
module \布尔表达式  (
  input  A,
  input  B,
  input  C,
  output F
);

  wire and_1_out, and_2_out, and_3_out;

  and and_1 (and_1_out, A, B);
  and and_2 (and_2_out, A, C);
  and and_3 (and_3_out, B, C);
  or or_1 (F, and_1_out, and_2_out, and_3_out);

  // Notes on the sheet:
  //   输入引脚
  //   请勿增加、删除引脚，用隧道标签构建电路
  //   请勿更改电路封装外观
  //   输出引脚
  //   武汉纺织大学数字逻辑课程组
endmodule

// Truth
module \真值表  (
  input  A,
  input  B,
  input  C,
  output F
);

  wire and_1_out, and_2_out, not_1_out, not_2_out, not_3_out;

  not not_1 (not_1_out, A);
  not not_2 (not_2_out, B);
  not not_3 (not_3_out, C);
  and and_1 (and_1_out, A, B, C);
  and and_2 (and_2_out, not_1_out, not_2_out, not_3_out);
  or or_1 (F, and_1_out, and_2_out);

  // Notes on the sheet:
  //   输入引脚
  //   请勿增加、删除引脚，用隧道标签构建电路
  //   请勿更改电路封装外观
  //   输出引脚
  //   武汉纺织大学数字逻辑课程组
endmodule

// sTruth
module \简化真值表  (
  input  X1,
  input  X0,
  input  Y1,
  input  Y0,
  output Gt
);

  wire and_1_out, and_2_out, and_3_out, not_1_out, not_2_out, not_3_out, not_4_out, not_5_out;

  not not_1 (not_1_out, Y1);
  not not_2 (not_2_out, Y0);
  not not_3 (not_3_out, X1);
  not not_4 (not_4_out, Y1);
  not not_5 (not_5_out, Y0);
  and and_1 (and_1_out, X1, not_1_out);
  and and_2 (and_2_out, X1, X0, Y1, not_2_out);
  and and_3 (and_3_out, not_3_out, X0, not_4_out, not_5_out);
  or or_1 (Gt, and_1_out, and_2_out, and_3_out);

  // Notes on the sheet:
  //   输入引脚
  //   请勿增加、删除引脚，用隧道标签构建电路
  //   请勿更改电路封装外观
  //   输出引脚
  //   武汉纺织大学数字逻辑课程组
endmodule

// Wave
module \波形图  (
  input  A,
  input  B,
  input  C,
  output F
);

  wire and_1_out, and_2_out, and_3_out, not_1_out, not_2_out, not_3_out, or_1_out;

  not not_1 (not_1_out, A);
  or or_1 (or_1_out, B, C);
  not not_2 (not_2_out, B);
  not not_3 (not_3_out, C);
  and and_1 (and_1_out, not_1_out, or_1_out);
  and and_2 (and_2_out, A, B, C);
  and and_3 (and_3_out, A, not_2_out, not_3_out);
  or or_2 (F, and_1_out, and_2_out, and_3_out);

  // Notes on the sheet:
  //   输入引脚
  //   A
  //   B
  //   C
  //   F
  //   请勿增加、删除引脚，用隧道标签构建电路
  //   请勿更改电路封装外观
  //   输出引脚
  //   武汉纺织大学数字逻辑课程组
endmodule

// Kmap
module \卡诺图  (
  input  A,
  input  B,
  input  C,
  input  D,
  output F
);

  wire not_1_out, not_2_out, not_3_out, not_4_out, or_1_out, or_2_out;

  not not_1 (not_1_out, A);
  not not_2 (not_2_out, C);
  not not_3 (not_3_out, B);
  not not_4 (not_4_out, D);
  or or_1 (or_1_out, not_1_out, not_2_out);
  or or_2 (or_2_out, not_3_out, not_4_out);
  and and_1 (F, or_1_out, or_2_out);

  // Notes on the sheet:
  //   输入引脚
  //   请勿增加、删除引脚，用隧道标签构建电路
  //   请勿更改电路封装外观
  //   输出引脚
  //   武汉纺织大学数字逻辑课程组
endmodule
