// Logisim project Register.circ as structural Verilog: 5 circuits, main circuit 基本寄存器
module \基本寄存器  (
  input  Clock,
  input  Reset,
  input  [3:0] Din,
  output [3:0] Q
);

  D_Flip_Flop FF3 (.clk(Clock), .D(Din[3]), .Q(Q[3]), .reset(Reset));  // open: Qn, preset, en
  D_Flip_Flop FF2 (.clk(Clock), .D(Din[2]), .Q(Q[2]), .reset(Reset));  // open: Qn, preset, en
  D_Flip_Flop FF1 (.clk(Clock), .D(Din[1]), .Q(Q[1]), .reset(Reset));  // open: Qn, preset, en
  D_Flip_Flop FF0 (.clk(Clock), .D(Din[0]), .Q(Q[0]), .reset(Reset));  // open: Qn, preset, en

  // Other names for the same wires on the sheet: D0 = Din[0]; D1 = Din[1]; D2 = Din[2]; D3 = Din[3]

  // Notes on the sheet:
  //   输入引脚
  //   请勿更改引脚区，直接用隧道标签构建4位基本寄存器电路！
  //   输出引脚
  //   武汉纺织大学数字逻辑课程组
endmodule

module \移位寄存器_右移  (
  input  Clock,
  input  Reset,
  input  In,
  output Out
);

  wire Q1, Q2, Q3;

  D_Flip_Flop FF3 (.clk(Clock), .D(In), .Q(Q3), .reset(Reset));  // open: Qn, preset, en
  D_Flip_Flop FF2 (.clk(Clock), .D(Q3), .Q(Q2), .reset(Reset));  // open: Qn, preset, en
  LED led_1 (.in(Q2));
  LED led_2 (.in(Q3));
  D_Flip_Flop FF1 (.clk(Clock), .D(Q2), .Q(Q1), .reset(Reset));  // open: Qn, preset, en
  LED led_3 (.in(Q1));
  LED led_4 (.in(Out));
  D_Flip_Flop FF0 (.clk(Clock), .D(Q1), .Q(Out), .reset(Reset));  // open: Qn, preset, en

  // Notes on the sheet:
  //   输入引脚
  //   请勿更改引脚区，直接用隧道标签构建4位右移移位寄存器电路！
  //   输出引脚
  //   武汉纺织大学数字逻辑课程组
endmodule

module \循环右移寄存器  (
  input  Clock,
  input  Reset,
  input  [3:0] Din,
  input  Load,
  output Out
);

  wire FF1_q, FF2_q, FF3_q, multiplexer_1_out, multiplexer_2_out, multiplexer_3_out, multiplexer_4_out;

  Multiplexer #(.enable("false")) multiplexer_1 (.in0(Out), .in1(Din[3]), .out(multiplexer_1_out), .sel(Load));
  LED led_1 (.in(FF3_q));
  D_Flip_Flop FF3 (.clk(Clock), .D(multiplexer_1_out), .Q(FF3_q), .reset(Reset));  // open: Qn, preset, en
  Multiplexer #(.enable("false")) multiplexer_2 (.in0(FF3_q), .in1(Din[2]), .out(multiplexer_2_out), .sel(Load));
  LED led_2 (.in(FF2_q));
  D_Flip_Flop FF2 (.clk(Clock), .D(multiplexer_2_out), .Q(FF2_q), .reset(Reset));  // open: Qn, preset, en
  Multiplexer #(.enable("false")) multiplexer_3 (.in0(FF2_q), .in1(Din[1]), .out(multiplexer_3_out), .sel(Load));
  LED led_3 (.in(FF1_q));
  D_Flip_Flop FF1 (.clk(Clock), .D(multiplexer_3_out), .Q(FF1_q), .reset(Reset));  // open: Qn, preset, en
  LED led_4 (.in(Out));
  D_Flip_Flop FF0 (.clk(Clock), .D(multiplexer_4_out), .Q(Out), .reset(Reset));  // open: Qn, preset, en
  Multiplexer #(.enable("false")) multiplexer_4 (.in0(FF1_q), .in1(Din[0]), .out(multiplexer_4_out), .sel(Load));

  // Other names for the same wires on the sheet: D0 = Din[0]; D1 = Din[1]; D2 = Din[2]; D3 = Din[3]

  // Notes on the sheet:
  //   输入引脚
  //   请勿更改引脚区，直接用隧道标签构建4位循环右移寄存器电路！
  //   武汉纺织大学数字逻辑课程组
  //   输出引脚
endmodule

module \并行存取的移位寄存器  (
  input  Reset,
  input  Clock,
  input  nShift_Load,
  input  [3:0] Din,
  input  SerialIn,
  output SerialOut,
  output [3:0] Q
);

  wire multiplexer_1_out, multiplexer_2_out, multiplexer_3_out, multiplexer_4_out;

  Multiplexer #(.enable("false")) multiplexer_1 (
    .in0(SerialIn), .in1(Din[3]), .out(multiplexer_1_out), .sel(nShift_Load));
  LED led_1 (.in(Q[3]));
  D_Flip_Flop FF3 (.clk(Clock), .D(multiplexer_1_out), .Q(Q[3]), .reset(Reset));  // open: Qn, preset, en
  LED led_2 (.in(Q[2]));
  D_Flip_Flop FF2 (.clk(Clock), .D(multiplexer_2_out), .Q(Q[2]), .reset(Reset));  // open: Qn, preset, en
  Multiplexer #(.enable("false")) multiplexer_2 (.in0(Q[3]), .in1(Din[2]), .out(multiplexer_2_out), .sel(nShift_Load));
  Multiplexer #(.enable("false")) multiplexer_3 (.in0(Q[2]), .in1(Din[1]), .out(multiplexer_3_out), .sel(nShift_Load));
  LED led_3 (.in(Q[1]));
  D_Flip_Flop FF1 (.clk(Clock), .D(multiplexer_3_out), .Q(Q[1]), .reset(Reset));  // open: Qn, preset, en
  Multiplexer #(.enable("false")) multiplexer_4 (.in0(Q[1]), .in1(Din[0]), .out(multiplexer_4_out), .sel(nShift_Load));
  LED led_4 (.in(Q[0]));
  D_Flip_Flop FF0 (.clk(Clock), .D(multiplexer_4_out), .Q(Q[0]), .reset(Reset));  // open: Qn, preset, en

  assign SerialOut = Q[0];

  // Other names for the same wires on the sheet: D0 = Din[0]; D1 = Din[1]; D2 = Din[2]; D3 = Din[3]

  // Notes on the sheet:
  //   输入引脚
  //   请勿更改引脚区，直接用隧道标签构建4位并行存取的右移寄存器电路！
  //   武汉纺织大学数字逻辑课程组
  //   输出引脚
endmodule

module \节拍脉冲发生器  (
  input  Clock,
  input  Start,
  output [3:0] T
);

  wire not_1_out;

  not not_1 (not_1_out, Start);
  LED led_1 (.in(T[0]));
  D_Flip_Flop d_ff_1 (.clk(Clock), .D(T[3]), .Q(T[0]), .preset(not_1_out));  // open: Qn, en, reset
  LED led_2 (.in(T[1]));
  D_Flip_Flop d_ff_2 (.clk(Clock), .D(T[0]), .Q(T[1]), .reset(not_1_out));  // open: Qn, preset, en
  LED led_3 (.in(T[2]));
  D_Flip_Flop d_ff_3 (.clk(Clock), .D(T[1]), .Q(T[2]), .reset(not_1_out));  // open: Qn, preset, en
  LED led_4 (.in(T[3]));
  D_Flip_Flop d_ff_4 (.clk(Clock), .D(T[2]), .Q(T[3]), .reset(not_1_out));  // open: Qn, preset, en

  // Notes on the sheet:
  //   输入引脚
  //   波形监测区
  //   请勿更改引脚区，直接用隧道标签构建4位独热码环形计数器（节拍脉冲发生器）电路！
  //   武汉纺织大学数字逻辑课程组
  //   输出引脚
endmodule
