// Logisim project Timer24.circ as structural Verilog: 6 circuits, main circuit 计时器
// 16
module \_4位递增计数器  (
  input  Clock,
  input  [3:0] D,
  input  Load,
  input  Enable,
  input  Reset,
  output [3:0] Q
);

  wire and_1_out, and_2_out, and_3_out, multiplexer_1_out, multiplexer_2_out, multiplexer_3_out,
       multiplexer_4_out, xor_1_out, xor_2_out, xor_3_out, xor_4_out;

  and and_1 (and_1_out, Enable, Q[0]);
  and and_2 (and_2_out, and_1_out, Q[1]);
  and and_3 (and_3_out, and_2_out, Q[2]);
  // AND_Gate and_4 has open pins: in0=and_3_out, in1=Q[3], out=open
  xor xor_1 (xor_1_out, Q[0], Enable);
  xor xor_2 (xor_2_out, Q[1], and_1_out);
  xor xor_3 (xor_3_out, Q[2], and_2_out);
  xor xor_4 (xor_4_out, Q[3], and_3_out);
  Multiplexer #(.enable("false")) multiplexer_1 (.in0(xor_1_out), .in1(D[0]), .out(multiplexer_1_out), .sel(Load));
  Multiplexer #(.enable("false")) multiplexer_2 (.in0(xor_2_out), .in1(D[1]), .out(multiplexer_2_out), .sel(Load));
  Multiplexer #(.enable("false")) multiplexer_3 (.in0(xor_3_out), .in1(D[2]), .out(multiplexer_3_out), .sel(Load));
  Multiplexer #(.enable("false")) multiplexer_4 (.in0(xor_4_out), .in1(D[3]), .out(multiplexer_4_out), .sel(Load));
  D_Flip_Flop d_ff_1 (.clk(Clock), .D(multiplexer_1_out), .Q(Q[0]), .reset(Reset));  // open: Qn, preset, en
  D_Flip_Flop d_ff_2 (.clk(Clock), .D(multiplexer_2_out), .Q(Q[1]), .reset(Reset));  // open: Qn, preset, en
  D_Flip_Flop d_ff_3 (.clk(Clock), .D(multiplexer_3_out), .Q(Q[2]), .reset(Reset));  // open: Qn, preset, en
  D_Flip_Flop d_ff_4 (.clk(Clock), .D(multiplexer_4_out), .Q(Q[3]), .reset(Reset));  // open: Qn, preset, en
  Hex_Digit_Display hex_digit_display_1 (.value(Q));  // open: dp

  // Notes on the sheet:
  //   输入引脚
  //   4位二进制（十六进制）同步置数、异步清零功能的同步递增计数器
  //   输出引脚
  //   请勿更改封装外观，否则无法完成测试
  //   监控区
endmodule

// 6
module \六进制计数器  (
  input  Clock,
  input  [3:0] D,
  input  Load,
  input  Enable,
  input  Reset,
  output Co,
  output [3:0] Q
);

  wire and_1_out, or_1_out;

  \_4位递增计数器  \u_4位递增计数器_1  (.Clock(Clock), .Enable(Enable), .Reset(or_1_out), .Q(Q), .D(D), .Load(Load));
  or or_1 (or_1_out, Reset, and_1_out);
  and and_1 (and_1_out, Q[2], Q[1]);
  Hex_Digit_Display hex_digit_display_1 (.value(Q));  // open: dp
  and and_2 (Co, Q[2], Q[0]);

  // Notes on the sheet:
  //   输入引脚
  //   六进制计数器
  //   输出引脚
  //   请勿更改封装外观，否则无法完成测试
  //   监控区
endmodule

// 10
module \十进制计数器  (
  input  Clock,
  input  [3:0] D,
  input  Load,
  input  Enable,
  input  Reset,
  output Co,
  output [3:0] Q
);

  wire and_1_out, or_1_out;

  \_4位递增计数器  \u_4位递增计数器_1  (.Clock(Clock), .Enable(Enable), .Reset(or_1_out), .Q(Q), .D(D), .Load(Load));
  or or_1 (or_1_out, Reset, and_1_out);
  and and_1 (and_1_out, Q[3], Q[1]);
  Hex_Digit_Display hex_digit_display_1 (.value(Q));  // open: dp
  and and_2 (Co, Q[0], Q[3]);

  // Notes on the sheet:
  //   输入引脚
  //   十进制计数器
  //   输出引脚
  //   请勿更改封装外观，否则无法完成测试
  //   监控区
endmodule

// 60
module \六十进制计数器  (
  input  Clock,
  input  [3:0] D1,
  input  Load,
  input  Enable,
  input  [3:0] D0,
  input  Reset,
  output Co,
  output [3:0] Q1,
  output [3:0] Q0
);

  wire and_1_out, \六进制计数器_1_co , \十进制计数器_1_co ;

  and and_1 (and_1_out, Enable, \十进制计数器_1_co );
  \六进制计数器  \u_六进制计数器_1  (
    .Clock(Clock), .D(D1), .Load(Load), .Enable(and_1_out), .Reset(Reset), .Co(\六进制计数器_1_co ), .Q(Q1));
  \十进制计数器  \u_十进制计数器_1  (
    .Clock(Clock), .Enable(Enable), .Reset(Reset), .Co(\十进制计数器_1_co ), .Q(Q0), .Load(Load), .D(D0));
  Hex_Digit_Display hex_digit_display_1 (.value(Q1));  // open: dp
  and and_2 (Co, \十进制计数器_1_co , \六进制计数器_1_co );
  Hex_Digit_Display hex_digit_display_2 (.value(Q0));  // open: dp

  // Notes on the sheet:
  //   输入引脚
  //   六十进制计数器
  //   输出引脚
  //   请勿更改封装外观，否则无法完成测试
  //   监控区
endmodule

// 24
module \二十四进制计数器  (
  input  Clock,
  input  [3:0] D1,
  input  Load,
  input  Enable,
  input  [3:0] D0,
  input  Reset,
  output Co,
  output [3:0] Q1,
  output [3:0] Q0
);

  wire and_1_out, and_2_out, or_1_out, \十进制计数器_2_co ;

  and and_1 (and_1_out, \十进制计数器_2_co , Enable);
  \十进制计数器  \u_十进制计数器_1  (.Clock(Clock), .Enable(and_1_out), .Reset(or_1_out), .Q(Q1), .Load(Load), .D(D1));  // open: Co
  \十进制计数器  \u_十进制计数器_2  (
    .Clock(Clock), .Enable(Enable), .Reset(or_1_out), .Co(\十进制计数器_2_co ), .Q(Q0), .Load(Load), .D(D0));
  or or_1 (or_1_out, Reset, and_2_out);
  and and_2 (and_2_out, Q0[2], Q1[1]);
  Hex_Digit_Display hex_digit_display_1 (.value(Q1));  // open: dp
  Hex_Digit_Display hex_digit_display_2 (.value(Q0));  // open: dp
  and and_3 (Co, Q1[1], Q0[1], Q0[0]);

  // Notes on the sheet:
  //   输入引脚
  //   二十四进制计数器
  //   输出引脚
  //   请勿更改封装外观，否则无法完成测试
  //   监控区
endmodule

module \计时器  (
  input  Clock,
  input  Load,
  input  [3:0] Dh1,
  input  [3:0] Dh0,
  input  [3:0] Dm1,
  input  [3:0] Dm0,
  input  [3:0] Ds1,
  input  [3:0] Ds0,
  input  Enable,
  input  Reset,
  output [3:0] H1,
  output [3:0] H0,
  output [3:0] M1,
  output [3:0] M0,
  output [3:0] S1,
  output [3:0] S0
);

  wire and_1_out, and_2_out, \六十进制计数器_1_co , \六十进制计数器_2_co ;

  Hex_Digit_Display hex_digit_display_1 (.value(H1));  // open: dp
  Hex_Digit_Display hex_digit_display_2 (.value(H0));  // open: dp
  Hex_Digit_Display hex_digit_display_3 (.value(M1));  // open: dp
  and and_1 (and_1_out, Enable, \六十进制计数器_2_co , \六十进制计数器_1_co );
  Hex_Digit_Display hex_digit_display_4 (.value(M0));  // open: dp
  \二十四进制计数器  \u_二十四进制计数器_1  (
    .Clock(Clock), .D1(Dh1), .Load(Load), .Q1(H1), .Q0(H0), .Enable(and_1_out), .D0(Dh0), .Reset(Reset));  // open: Co
  Hex_Digit_Display hex_digit_display_5 (.value(S1));  // open: dp
  Hex_Digit_Display hex_digit_display_6 (.value(S0));  // open: dp
  \六十进制计数器  \u_六十进制计数器_1  (
    .Co(\六十进制计数器_1_co ), .Q1(M1), .Q0(M0), .Clock(Clock), .D1(Dm1), .Load(Load), .Enable(and_2_out),
    .Reset(Reset), .D0(Dm0));
  and and_2 (and_2_out, Enable, \六十进制计数器_2_co );
  \六十进制计数器  \u_六十进制计数器_2  (
    .Co(\六十进制计数器_2_co ), .Q1(S1), .Q0(S0), .Clock(Clock), .D1(Ds1), .Load(Load), .Enable(Enable),
    .Reset(Reset), .D0(Ds0));

  // Notes on the sheet:
  //   二十四小时计时器
  //   :
  //   输入引脚
  //   :
  //   请勿更改封装外观，否则无法完成测试
  //   输出引脚
endmodule
